# Fritzing sketch hardware_plan (saved by Fritzing 0.9.3b)
breadboards: 2

parts:
  U2 = TRANSISTOR_NPN_2 [package=to-92]
  R1 = Resistor [tolerance=±5% resistance=5k package=THT]
  U3 = TRANSISTOR_NPN_2 [package=to-92]
  R2 = Resistor [tolerance=±5% resistance=220 package=THT]
  R3 = Resistor [tolerance=±5% resistance=220 package=THT]
  R4 = Resistor [tolerance=±5% resistance=220 package=THT]
  R5 = Resistor [tolerance=±5% resistance=220 package=THT]
  C1 = Electrolytic Capacitor [capacitance=10μF package="0605 [SMD, electrolytic]"]
  R6 = Resistor [tolerance=±5% resistance=220 package="0402 [SMD]"]
  R7 = Resistor [tolerance=±5% resistance=220 package="0402 [SMD]"]
  U4 = TRANSISTOR_NPN_2 [package=to-92]
  R8 = Resistor [tolerance=±5% resistance=220 package="0402 [SMD]"]
  R9 = Resistor [tolerance=±5% resistance=220 package="0402 [SMD]"]
  C2 = Electrolytic Capacitor [capacitance=10μF package="0605 [SMD, electrolytic]"]
  R10 = Resistor [tolerance=±5% resistance=220 package="0402 [SMD]"]
  U5 = OP27 - Low Noise, Precision Op Amp [part_number=OP27]
  R11 = Resistor [tolerance=±5% resistance=220 package="0402 [SMD]"]
  C3 = Electrolytic Capacitor [capacitance=10μF package="0605 [SMD, electrolytic]"]

nets:
  N1: U2.C, R2.Pin_0
  N2: U2.E, R4.Pin_1
  N3: R1.Pin_0, U3.C
  N4: R1.Pin_1, R2.Pin_1, C1.-, R7.Pin_1, R8.Pin_1
  N5: U3.E, R3.Pin_0
  N6: R3.Pin_1, R4.Pin_0, R5.Pin_0
  N7: R5.Pin_1, R6.Pin_0, R9.Pin_1
  N8: C1.+, R6.Pin_1, R7.Pin_0, U4.B
  N9: U4.C, R8.Pin_0, C2.-
  N10: U4.E, R9.Pin_0
  N11: C2.+, R10.Pin_0
  N12: R10.Pin_1, U5.-IN, R11.Pin_1
  N13: U5.OUT, R11.Pin_0, C3.-, C3.+
